// Logisim project bleh.circ as structural Verilog: 1 circuit, main circuit main
module main (
);

  wire clock_1_out, not_1_out;
  wire [3:0] adder_1_out, register_1_q, register_2_q;

  Clock clock_1 (.out(clock_1_out));
  not not_1 (not_1_out, clock_1_out);
  Register #(.width(4), .trigger("high")) register_1 (
    .D(register_2_q), .en(clock_1_out), .Q(register_1_q));  // open: clk, clr
  Register #(.width(4), .trigger("high")) register_2 (
    .D(adder_1_out), .en(not_1_out), .Q(register_2_q));  // open: clk, clr
  Adder #(.width(4)) adder_1 (.a(register_1_q), .b(4'b0001), .out(adder_1_out));  // open: cin, cout
  Comparator #(.width(4)) comparator_1 ();  // open: a, b, gt, eq, lt
endmodule
