// Logisim project lab-7_q.circ as structural Verilog: 2 circuits, main circuit clk_2phase
module main (
);

  clk_2phase clk_2phase_1 ();  // open: phi_1, phi_2
endmodule

// CLK
module clk_2phase (
  output phi_1,
  output phi_2
);

  wire clock_1_out, nand_1_out, nand_2_out, not_1_out, not_2_out, not_3_out;

  Clock clock_1 (.out(clock_1_out));
  not not_1 (not_1_out, clock_1_out);
  nand nand_1 (nand_1_out, not_1_out, phi_2);
  not not_2 (not_2_out, nand_1_out);
  not not_3 (not_3_out, nand_2_out);
  nand nand_2 (nand_2_out, phi_1, clock_1_out);
  not not_4 (phi_1, not_2_out);
  not not_5 (phi_2, not_3_out);
endmodule
